# Fritzing sketch esp8266-hc-sr04 (saved by Fritzing 0.9.3b)
breadboards: 1

parts:
  Part1 = SRF05 Ultrasonic Rangefinder
  U1 = NodeMCU V3.0

nets:
  VCC: Part1.VCC, U1.Vin
  N1: Part1.Trig, U1.D1
  N2: Part1.Echo, U1.D2
  N3: Part1.GND, U1.GND#6, U1.GND#13, U1.GND#16, U1.GND#33

custom parts:
  NodeMCU V3.0: ESP8266 based NodeMCU
